# Fritzing sketch senzor server (saved by Fritzing 0.9.3b)
breadboards: 1

parts:
  WeMos_D1_Mini1 = WeMos D1 Mini
  Součástka2 = NRF24L01
  IC2 = Voltage Regulator AMS1117 [package=sot223]
  DS7 = DS18B20 1-Wire Temperature Sensor [part_number=DS18B20]
  R2 = Resistor [tolerance=±5% resistance=4.7k package="2010 [SMD]"]
  R3 = Resistor [tolerance=±5% resistance=4.7k package="2010 [SMD]"]

nets:
  N1: WeMos_D1_Mini1.5V, IC2.IN
  N2: WeMos_D1_Mini1.D1, DS7.DQ, R2.Pin_0
  N3: WeMos_D1_Mini1.D4, Součástka2.CE
  N4: WeMos_D1_Mini1.D5, Součástka2.SCK
  N5: WeMos_D1_Mini1.D6, Součástka2.MISO
  N6: WeMos_D1_Mini1.D7, Součástka2.MOSI
  N7: WeMos_D1_Mini1.D8, Součástka2.CSN, R3.Pin_0
  GND: WeMos_D1_Mini1.G, Součástka2.GND, IC2.GND, DS7.GND, R3.Pin_1
  N8: Součástka2.VCC, IC2.OUT
  N9: DS7.VDD, R2.Pin_1
